# Fritzing sketch Untitled Sketch 2 (saved by Fritzing 0.9.4)
breadboards: 1

parts:
  Parça1 = Arduino Uno (Rev3)
  LCD1 = LCD screen
  LED1 = RGB LED (com. cathode, rgb) [package="5 mm [THT]"]
  R1 = Resistor [tolerance=±5% resistance=220 package=THT]
  R2 = Resistor [tolerance=±5% resistance=220 package=THT]
  R3 = Resistor [tolerance=±5% resistance=220 package=THT]
  T1 = LM35 Temperature Sensor [package="TO92 [THT]"]
  R4 = Rotary Potentiometer (Small) [maximum_resistance=100kΩ package=THT]

nets:
  N1: Parça1.A0, T1.Vout
  N2: Parça1.D8, LCD1.E
  N3: Parça1.D9_PWM, R3.Pin_1
  N4: Parça1.D10_PWM/SS, R2.Pin_1
  N5: Parça1.D11_PWM/MOSI, R1.Pin_1
  N6: Parça1.D12/MISO, LCD1.RS
  N7: Parça1.D2, LCD1.DB7
  N8: Parça1.D3_PWM, LCD1.DB6
  N9: Parça1.D4, LCD1.DB5
  N10: Parça1.D5_PWM, LCD1.DB4
  N11: Parça1.5V, LED1.common_cathode, T1.+Vs, R4.leg1, R4.leg2
  GND: Parça1.GND, T1.GND
  N12: LCD1.VSS, LCD1.R/W, LCD1.LED-
  N13: LCD1.VDD, LCD1.LED+
  N14: LCD1.V0, R4.wiper
  N15: LED1.red_anode, R1.Pin_0
  N16: LED1.green_anode, R2.Pin_0
  N17: LED1.blue_anode, R3.Pin_0
